# Fritzing sketch input-output-demo (saved by Fritzing 0.9.2b)
breadboards: 1

parts:
  Part1 = Arduino Uno (Rev3)
  R1 = Trimmer Potentiometer [maximum_resistance=10kΩ package=THT]
  S1 = Pushbutton [package="[THT]"]
  R2 = Resistor [tolerance=±5% resistance=220 package=THT]
  LED1 = LED - 5mm [color="Red (633nm)" package="5 mm [THT]"]
  R3 = Resistor [tolerance=±5% resistance=220 package=THT]
  LED2 = LED - 5mm [color="Red (633nm)" package="5 mm [THT]"]
  Part2 = KY-004 Key Switch Module [package="Breakout board"]

nets:
  N1: Part1.A0, R1.wiper
  N2: Part1.D2, LED1.anode
  N3: Part1.D3_PWM, LED2.anode
  N4: Part1.D5_PWM, Part2.S
  N5: Part1.D6_PWM, S1.Pin_1, S1.Pin_2
  5V: Part1.5V, R1.leg2, Part2.Vin
  N6: Part1.GND, R1.leg1, S1.Pin_3, S1.Pin_4, R2.Pin_0, R3.Pin_1, Part2.-
  N7: R2.Pin_1, LED1.cathode
  N8: R3.Pin_0, LED2.cathode

custom parts:
  KY-004 Key Switch Module: Arduino Key Switch Module Keyes KY-004 is a push button that will output a high signal when pressed.
